# Fritzing sketch RTKBaseStation (saved by Fritzing 0.9.9b)
breadboards: 1

parts:
  Part1 = Adafruit HUZZAH32 ESP32 Feather [part_number="Adafruit #3405"]
  Qwiic1_RTK-SMA = Qwiic Connector  # not connected
  10_k = Resistor [tolerance=±5% power=0.25 resistance=220 package=THT]
  S1 = Pushbutton [package="[SMD]"]
  BAT1 = Battery Holders [package=lipo-1100mAh]
  Qwiic2_Oled_Display_attached_on_RTK2_module = Qwiic Connector  # not connected

nets:
  N1: Part1.GND, 10_k.Pin_1, BAT1.-
  N2: Part1.3.3V, S1.Pin_1, S1.Pin_2
  N3: Part1.VBAT, BAT1.+
  N4: Part1.IO15_A8, 10_k.Pin_0, S1.Pin_3, S1.Pin_4

custom parts:
  Qwiic Connector: Qwiic PCB connector
